# Fritzing sketch Wiring (saved by Fritzing 0.9.0b)
circuit board: 8.46667cm x 5.64444cm
breadboards: 1

parts:
  VCC1 = Battery block 9V
  Top_Left_LDR = Photocell (LDR) [package=THT]
  Top_Right_LDR = Photocell (LDR) [package=THT]
  Bottom_Left_LDR = Photocell (LDR) [package=THT]
  Bottom_Right_LDR = Photocell (LDR) [package=THT]
  R6 = Resistor [tolerance=±5% resistance=220 package=THT]
  R7 = Resistor [tolerance=±5% resistance=220 package=THT]
  R8 = Resistor [tolerance=±5% resistance=220 package=THT]
  R9 = Resistor [tolerance=±5% resistance=220 package=THT]
  DC_MOTOR_VERTICAL = DC Motor
  IC2 = L293D [package=THT]
  DC_MOTOR_HORIZONTAL = DC Motor
  Part1 = Arduino Leonardo (Rev3b)

nets:
  N1: VCC1.-, IC2.0V, Part1.GND
  N2: VCC1.+, IC2.Enable_1, IC2.+Vmotor, IC2.Enable_2, IC2.+V
  N3: Top_Left_LDR.pin_0, R6.Pin_1, Part1.A0
  N4: Top_Right_LDR.pin_0, R7.Pin_1, Part1.A1
  N5: Bottom_Left_LDR.pin_0, R8.Pin_1, Part1.A2
  N6: Bottom_Right_LDR.pin_0, R9.Pin_1, Part1.A3
  N7: Bottom_Right_LDR.pin_1, Part1.5V
  N8: DC_MOTOR_VERTICAL.pin_1, IC2.Out_4_(_Controlled_by_Enable_2_)
  N9: DC_MOTOR_VERTICAL.pin_2, IC2.Out_3_(_Controlled_by_Enable_2_)
  N10: IC2.In_1, Part1.D9_PWM/A9
  N11: IC2.Out_1_(_Controlled_by_Enable_1_), DC_MOTOR_HORIZONTAL.pin_1
  N12: IC2.Out_2_(_Controlled_by_Enable_1_), DC_MOTOR_HORIZONTAL.pin_2
  N13: IC2.In_2, Part1.D8/A8
  N14: IC2.In_3, Part1.D6_PWM/A7
  N15: IC2.In_4, Part1.D7
